# Fritzing sketch usbKatana_Expression_MIDIthrogh (saved by Fritzing 0.9.3b)
breadboards: 1

parts:
  DIN1 = DIN-5 jack (MIDI) [package=THT]  # not connected
  S1 = Pushbutton [package="[SMD]"]
  S2 = Pushbutton [package="[SMD]"]
  R3 = Resistor [tolerance=±5% resistance=220 package="0603 [SMD]"]
  LED2 = LEDs [package=led10mm]
  R4 = Resistor [tolerance=±5% resistance=220 package="0603 [SMD]"]
  LED1 = LEDs [package=led10mm]
  S3 = Pushbutton [package="[SMD]"]
  S4 = Pushbutton [package="[SMD]"]
  LED3 = LEDs [package=led10mm]
  R7 = Resistor [tolerance=±5% resistance=220 package="0603 [SMD]"]
  R8 = Resistor [tolerance=±5% resistance=220 package="0603 [SMD]"]
  LED4 = LEDs [package=led10mm]
  Teensy_3_1 = Teensy 3.1
  R9 = Resistor [tolerance=±5% resistance=220 package="0603 [SMD]"]
  S5 = Pushbutton [package="[SMD]"]
  LED5 = LEDs [package=led10mm]
  LCD1 = LCD screen  # not connected
  DIN2 = DIN-5 jack (MIDI) [package=THT]  # not connected
  DIN3 = DIN-5 jack (MIDI) [package=THT]
  R10 = Resistor [tolerance=±5% resistance=220 package="0603 [SMD]"]  # not connected
  R11 = Resistor [tolerance=±5% resistance=220 package="0603 [SMD]"]  # not connected

nets:
  N1: S1.Pin_1, S1.Pin_2, S2.Pin_1, S2.Pin_2, R3.Pin_0, R4.Pin_0, S3.Pin_1, S3.Pin_2, S4.Pin_1, S4.Pin_2, R7.Pin_0, R8.Pin_0, Teensy_3_1.GND, R9.Pin_0, S5.Pin_1, S5.Pin_2, DIN3.2
  N2: S1.Pin_3, S1.Pin_4, Teensy_3_1.D2
  N3: S2.Pin_3, S2.Pin_4, Teensy_3_1.D3
  N4: R3.Pin_1, LED1.A
  N5: LED2.C, Teensy_3_1.A0/D14
  N6: LED2.A, R4.Pin_1
  N7: LED1.C, Teensy_3_1.A3/D17
  N8: S3.Pin_3, S3.Pin_4, Teensy_3_1.D4
  N9: S4.Pin_3, S4.Pin_4, Teensy_3_1.D5
  N10: LED3.C, Teensy_3_1.A1/D15
  N11: LED3.A, R7.Pin_1
  N12: R8.Pin_1, LED4.A
  N13: LED4.C, Teensy_3_1.A2/D16
  N14: Teensy_3_1.D6, S5.Pin_3, S5.Pin_4
  N15: Teensy_3_1.D7, LED5.C
  N16: R9.Pin_1, LED5.A

notes:
  MIDI Shield or I/O curcuit
  TX RX 5V GND
  I2C 20x4 LCD
  SDA SCL 5v GND
  USB mini host shield
  B Host Shield
  Teensy 3.0
  RESET
  3.3V
  GND
  GND
  INT
  9
  SS
  10
  MOSI
  11
  MISO
  12
  SCK
  13
  3.3V
  3.3V
  GND
  GND
  Connect 3.3v and GND as listed above.
  Teensy 3.2
  https://www.circuitsathome.com/mcu/teensy-3-0-now-supported-by-the-usb-host-library/
  https://www.circuitsathome.com/wp/wp-content/uploads/2011/02/uhm11_manual.jpg
  Wire expression pedal(s) here as shown:
  https://github.com/sixeight7/VController_v3/blob/master/Main%20board/VController%20main%20board.pdf
  Expression pedal 2 not tested
  MIDI Through (not tested)
  5v
  MIDI IN / OUT, through, and expression pedals optional.

// code stored in the sketch: Midi.v01.ino
// project from: https://www.makeuseof.com/tag/make-midi-controller-arduino/
// PC change command from: http://thoro.de/images/guitars/midi_mule/Schlueter_Midi_Mule_Script_v1.ino
// Some code from: https://www.morningstarfx.com/single-post/2016/07/17/Building-your-own-Arduinobased-Midi-Controller
// Wiring from: https://static.makeuseof.com/wp-content/uploads/2016/07/Arduino-Midi-Controller-Circuit.png


#include <MIDI.h>
#include <midi_Defs.h>
#include <midi_Message.h>
#include <midi_Namespace.h>
#include <midi_Settings.h>

#define TOTAL_LED 4

const int SW1 = 2; // assign button pin to variable
const int SW2 = 3; // assign button pin to variable
const int SW3 = 4; // assign button pin to variable
const int SW4 = 5; // assign button pin to variable

const int ledPin1 = 8;   // led pin -> LED-> 220k R-> ground
const int ledPin2 = 9;  // led pin -> LED-> 220k R-> ground
const int ledPin3 = 10;   // led pin -> LED-> 220k R-> ground
const int ledPin4 = 11;  // led pin -> LED-> 220k R-> ground

byte ledArray[] = {ledPin1, ledPin2, ledPin3, ledPin4};


// Loop to turn all LEDs off
void setAllLEDs(int type) {
  for (int i = 0; i < TOTAL_LED; i++) {
    digitalWrite(ledArray[i], type);
  }
}


// blink the leds at start up
void blinkAllLeds(unsigned long numTimes, unsigned long inDelay) {
  for (int j = 0; j < numTimes; j++) {
    for (int i = 0; i < TOTAL_LED; i++) {
      digitalWrite(ledArray[i], HIGH);
      delay(inDelay);
      digitalWrite(ledArray[i], LOW);
    }
  }
}



MIDI_CREATE_INSTANCE(HardwareSerial, Serial, midiOut); // create a MIDI object called midiOut

void setup() {
  pinMode(SW1, INPUT_PULLUP); // setup button as input
  pinMode(SW2, INPUT_PULLUP); // setup button as input
  pinMode(SW3, INPUT_PULLUP); // setup button as input
  pinMode(SW4, INPUT_PULLUP); // setup button as input
  Serial.begin(9600); // setup MIDI output
  pinMode(ledPin1, OUTPUT);
  pinMode(ledPin2, OUTPUT);
  pinMode(ledPin3, OUTPUT);
  pinMode(ledPin4, OUTPUT);

  // set to PC 0 and set LEDS
  midiOut.sendProgramChange(0, 1);
  blinkAllLeds(3, 200);
  digitalWrite (ledPin1, HIGH);
  digitalWrite (ledPin2, LOW);

}


unsigned long db = 100; // Variable for debounce
unsigned long lastRead = millis();
byte chn = 1; // Midi Channel


void loop() {
   // PC 0
  if (digitalRead(SW1) == LOW && millis() - lastRead > db) {
    setAllLEDs(LOW);
    digitalWrite(ledPin1, HIGH);
    midiOut.sendProgramChange(0,chn); // Send PC 0 to chanel 1
    lastRead = millis();
  }

  if (digitalRead(SW2) == LOW && millis() - lastRead > db) { // check button state -- LOW if using N.O. momentary footswitch
    delay(db); // software de-bounce
    if (digitalRead(SW2) == LOW) { // check button state again -- LOW if using N.O. momentary footswitch
      midiOut.sendProgramChange(1, chn); // Send PC 1 to chanel 1
      //digitalWrite (ledPin9, LOW);
      setAllLEDs(LOW);
      digitalWrite (ledPin2, HIGH);
      lastRead = millis();
    }
  }
  if (digitalRead(SW3) == LOW && millis() - lastRead > db) { // check button state
    delay(db); // software de-bounce
    if (digitalRead(SW3) == LOW) { // check button state again
      midiOut.sendProgramChange(3, chn); // Send PC 0 to chanel 1
      setAllLEDs(LOW);
      digitalWrite (ledPin3, HIGH);
      lastRead = millis();
    }
  }
    if (digitalRead(SW4) == LOW && millis() - lastRead > db) { // check button state
      delay(db); // software de-bounce
      if (digitalRead(SW4) == LOW) { // check button state again
        midiOut.sendProgramChange(4, chn); // Send PC 0 to chanel 1
        setAllLEDs(LOW);
        digitalWrite (ledPin4, HIGH);
        lastRead = millis();
      }
    }
  }

// code stored in the sketch: Midi_PC_chage_4SW_v1.0.ino
// project from: https://www.makeuseof.com/tag/make-midi-controller-arduino/
// PC change command from: http://thoro.de/images/guitars/midi_mule/Schlueter_Midi_Mule_Script_v1.ino
// Some code from: https://www.morningstarfx.com/single-post/2016/07/17/Building-your-own-Arduinobased-Midi-Controller
// Wiring from: https://static.makeuseof.com/wp-content/uploads/2016/07/Arduino-Midi-Controller-Circuit.png


#include <MIDI.h>
#include <midi_Defs.h>
#include <midi_Message.h>
#include <midi_Namespace.h>
#include <midi_Settings.h>
#include <Wire.h> 
#include <LiquidCrystal_I2C.h>


#define TOTAL_LED 4

const int SW1 = 2; // assign button pin to variable
const int SW2 = 3; // assign button pin to variable
const int SW3 = 4; // assign button pin to variable
const int SW4 = 5; // assign button pin to variable

const int ledPin1 = 8;   // led pin -> LED-> 220k R-> ground
const int ledPin2 = 9;  // led pin -> LED-> 220k R-> ground
const int ledPin3 = 10;   // led pin -> LED-> 220k R-> ground
const int ledPin4 = 11;  // led pin -> LED-> 220k R-> ground

byte ledArray[] = {ledPin1, ledPin2, ledPin3, ledPin4};


// Loop to turn all LEDs off
void setAllLEDs(int type) {
  for (int i = 0; i < TOTAL_LED; i++) {
    digitalWrite(ledArray[i], type);
  }
}


// blink the leds at start up
void blinkAllLeds(unsigned long numTimes, unsigned long inDelay) {
  for (int j = 0; j < numTimes; j++) {
    for (int i = 0; i < TOTAL_LED; i++) {
      digitalWrite(ledArray[i], HIGH);
      delay(inDelay);
      digitalWrite(ledArray[i], LOW);
    }
  }
}



MIDI_CREATE_INSTANCE(HardwareSerial, Serial, midiOut); // create a MIDI object called midiOut
LiquidCrystal_I2C lcd(0x27,20,4);  // set the LCD address to 0x27 for a 16 chars and 2 line display

void setup() {
  pinMode(SW1, INPUT_PULLUP); // setup button as input
  pinMode(SW2, INPUT_PULLUP); // setup button as input
  pinMode(SW3, INPUT_PULLUP); // setup button as input
  pinMode(SW4, INPUT_PULLUP); // setup button as input
  Serial.begin(31250); // setup MIDI output
  pinMode(ledPin1, OUTPUT);
  pinMode(ledPin2, OUTPUT);
  pinMode(ledPin3, OUTPUT);
  pinMode(ledPin4, OUTPUT);

  // set to PC 0 and set LEDS
  midiOut.sendProgramChange(0, 1);
  lcd.init();
  lcd.backlight();
  lcd.setCursor(0,0);
  lcd.print("Initializing...");
  blinkAllLeds(3, 200);
  digitalWrite (ledPin1, HIGH);
  digitalWrite (ledPin2, LOW);
  lcd.clear();
  lcd.setCursor(0,0);
  lcd.print("PC 1");
}


unsigned long db = 100; // Variable for debounce
unsigned long lastRead = millis();
byte chn = 3; // Midi Channel


void loop() {
  // PC 0
  if (digitalRead(SW1) == LOW && millis() - lastRead > db) {
    setAllLEDs(LOW);
    digitalWrite(ledPin1, HIGH);
    lcd.setCursor(0,0);
    lcd.print("PC 1");
    midiOut.sendProgramChange(0, chn); // Send PC 0 to chanel 1
    lastRead = millis();
  }

  if (digitalRead(SW2) == LOW && millis() - lastRead > db) {
    setAllLEDs(LOW);
    digitalWrite(ledPin2, HIGH);
    lcd.setCursor(0,0);
    lcd.print("PC 2");
    midiOut.sendProgramChange(1, chn); // Send PC 0 to chanel 1
    lastRead = millis();
  }
  if (digitalRead(SW3) == LOW && millis() - lastRead > db) {
    setAllLEDs(LOW);
    digitalWrite(ledPin3, HIGH);
    lcd.setCursor(0,0);
    lcd.print("PC 3");
    midiOut.sendProgramChange(2, chn); // Send PC 0 to chanel 1
    lastRead = millis();
  }

  if (digitalRead(SW4) == LOW && millis() - lastRead > db) {
    setAllLEDs(LOW);
    digitalWrite(ledPin4, HIGH);
    lcd.setCursor(0,0);
    lcd.print("PC 4");
    midiOut.sendProgramChange(3, chn); // Send PC 0 to chanel 1
    lastRead = millis();
  }
}
